# Fritzing sketch electronics0 (saved by Fritzing 1.0.4)
stripboards: 1

parts:
  Mod1 = Amica NodeMCU DEVKIT 1.0
  J2 = Basic Servo
  J3 = Dagu DGServo 9g header (male) [package=THT]
  J4 = male pin header, 2 pins [form="♂ (male)"]
  Yumo-enc1 = YumoE6B2
  J5 = male pin header, 4 pins [form="♂ (male)"]
  J6 = male pin header, 3 pins [form="♂ (male)"]
  J7 = female pin header, 2 pins [form="♀ (female)"]
  J9 = female pin header, 2 pins [form="♀ (female)"]
  J8 = female pin header, 3 pins [form="♀ (female)"]
  J10 = female pin header, 1 pin [form="♀ (female)"]

nets:
  3.3V: Mod1.pin1, Mod1.pin_10, Mod1.pin_26, J6.pin2, J8.pin2
  GND: Mod1.pin2, Mod1.pin_9, Mod1.pin_25, Mod1.pin_29, J2.gnd, J3.gnd, J4.pin1, Yumo-enc1.GND, J5.pin1, J6.pin1, J7.pin1, J8.pin3
  N1: Mod1.pin5, Yumo-enc1.B, J5.pin4, J9.pin2
  N2: Mod1.pin6, Yumo-enc1.A, J5.pin3, J9.pin1
  N3: Mod1.pin_11, J6.pin3, J8.pin1
  N4: Mod1.pin_15, J2.pulse, J3.pulse, J10.pin1
  6V: Mod1.pin_30, J2.vcc, J3.Vcc, J4.pin2, Yumo-enc1.V, J5.pin2, J7.pin2
